// Logisim project alu.circ as structural Verilog: 1 circuit, main circuit alu
module alu (
  input  [31:0] A,
  input  [31:0] B,
  input  [3:0] ALUSel,
  output [31:0] ALUResult
);

  wire comparator_1_lt;
  wire [31:0] add0, and0, mul0, mulh0, or0, Sll0, Slt0, sra0, srl0, sub0, xor0;

  assign and0 = A & B;  // AND_Gate and_1, 32 bits wide
  Multiplier #(.width(32)) multiplier_1 (.a(A), .b(B), .cout(mulh0));  // open: out, cin
  assign xor0 = A ^ B;  // XOR_Gate xor_1, 32 bits wide
  Shifter #(.width(32), .shift("lr")) shifter_1 (.in(A), .\dist (B[4:0]), .out(srl0));
  Adder #(.width(32)) adder_1 (.a(A), .b(B), .out(add0));  // open: cin, cout
  Shifter #(.width(32)) shifter_2 (.in(A), .\dist (B[4:0]), .out(Sll0));
  Comparator #(.width(32)) comparator_1 (.a(A), .b(B), .lt(comparator_1_lt));  // open: gt, eq
  assign or0 = A | B;  // OR_Gate or_1, 32 bits wide
  Multiplier #(.width(32)) multiplier_2 (.a(A), .b(B), .out(mul0));  // open: cin, cout
  Subtractor #(.width(32)) subtractor_1 (.a(A), .b(B), .out(sub0));  // open: bin, bout
  assign Slt0 = {{31{1'b0}}, comparator_1_lt};  // Bit_Extender bit_extender_1
  Multiplexer #(.select(4), .width(32), .enable("false")) multiplexer_1 (
    .in0(add0), .in1(Sll0), .in2(Slt0), .in4(xor0), .in5(srl0), .in6(or0), .in7(and0), .in8(mul0),
    .in9(mulh0), .in12(sub0), .in13(sra0), .out(ALUResult), .sel(ALUSel));  // open: in3, in10, in11, in14, in15
  Shifter #(.width(32), .shift("ar")) shifter_3 (.in(A), .\dist (B[4:0]), .out(sra0));

  // Notes on the sheet:
  //   INPUTS to your circuit
  //   DON'T CHANGE THE LOCATIONS OF THE INPUTS AND OUTPUTS!
  //   OUTPUT from your circuit
endmodule
