// Logisim project control-logic - R-type.circ as structural Verilog: 1 circuit, main circuit control_logic
module control_logic (
  input  [31:0] in_1,
  input  in_2,
  input  in_3,
  output out_4,
  output out_5,
  output [2:0] out_6,
  output out_7,
  output out_8,
  output out_9,
  output [3:0] out_10,
  output out_11,
  output [1:0] out_12
);

  wire mul0;
  wire [3:0] bit_extender_1_out;

  assign bit_extender_1_out = {{1{1'b0}}, in_1[14:12]};  // Bit_Extender bit_extender_1
  Comparator #(.width(7)) comparator_1 (.a(in_1[31:25]), .b(7'b0000001), .eq(mul0));  // open: gt, lt
  Multiplexer #(.width(4), .enable("false")) multiplexer_1 (
    .in0(bit_extender_1_out), .in1(4'b1000), .out(out_10), .sel(mul0));
  ROM #(.addrWidth(6), .dataWidth(16)) rom_1 ();  // open: addr, data

  assign in_1[19:15] = in_1[24:20];
  assign out_5 = 1'b1;

  // Other names for the same wires on the sheet: ImmSel[2:0] = out_6; BrUn = out_7; ASel = out_8; BSel = out_9;
  //   ALUSel[3:0] = out_10; MemWEn = out_11; WBSel[1:0] = out_12; BrEq = in_2; BrLt = in_3;
  //   Instruction[31:0] = {in_1[31:20], in_1[24:20], in_1[14:0]}; Opcode[6:0] = in_1[6:0]; rd[4:0] = in_1[11:7];
  //   func3[2:0] = in_1[14:12]; rs1[4:0] = in_1[24:20]; func7[6:0] = in_1[31:25]; PCSel = out_4

  // Notes on the sheet:
  //   INPUTS to your circuit
  //   Connect ROM Input here ->
  //   ROM FOR CONTROL LOGIC
  //   DON'T CHANGE THE LOCATIONS OF THE INPUTS AND OUTPUTS!
  //   This is only if you choose to do the ROM option
  //   OUTPUT from your circuit
  //   Reminder: If using ROM, use combinational logic for PCSel
endmodule
