// Logisim project regfile.circ as structural Verilog: 1 circuit, main circuit regfile
module regfile (
  input  [4:0] ReadIndex1,
  input  [4:0] ReadIndex2,
  input  [4:0] WriteIndex,
  input  [31:0] WriteData,
  input  RegWEn,
  input  clk,
  output [31:0] ra,
  output [31:0] sp,
  output [31:0] t0,
  output [31:0] t1,
  output [31:0] t2,
  output [31:0] s0,
  output [31:0] s1,
  output [31:0] a0,
  output [31:0] ReadData1,
  output [31:0] ReadData2
);

  wire a0w, raw, s0w, s1w, spw, t0w, t1w, t2w, x0w, x3w, x4w, x11w, x12w, x13w, x14w, x15w, x16w, x17w, x18w,
       x19w, x20w, x21w, x22w, x23w, x24w, x25w, x26w, x27w, x28w, x29w, x30w, x31w;
  wire [31:0] multiplexer_1_out, multiplexer_2_out, multiplexer_3_out, multiplexer_4_out, multiplexer_5_out,
       multiplexer_6_out, multiplexer_7_out, multiplexer_8_out, multiplexer_9_out, multiplexer_10_out,
       multiplexer_11_out, multiplexer_12_out, multiplexer_13_out, multiplexer_14_out, multiplexer_15_out,
       multiplexer_16_out, multiplexer_17_out, multiplexer_18_out, multiplexer_19_out, multiplexer_20_out,
       multiplexer_21_out, multiplexer_22_out, multiplexer_23_out, multiplexer_24_out, multiplexer_25_out,
       multiplexer_26_out, multiplexer_28_out, multiplexer_29_out, multiplexer_30_p3, multiplexer_31_out,
       multiplexer_33_p3, multiplexer_34_out, undriven, x0q, x3q, x4q, x11q, x12q, x13q, x14q, x15q, x16q,
       x17q, x18q, x19q, x20q, x21q, x22q, x23q, x24q, x25q, x26q, x27q, x28q, x29q, x30q, x31q;

  Demultiplexer #(.select(5), .enable("false")) demultiplexer_1 (
    .out0(x0w), .out1(raw), .out2(spw), .out3(x3w), .out4(x4w), .out5(t0w), .out6(t1w), .out7(t2w),
    .out8(s0w), .out9(s1w), .out10(a0w), .out11(x11w), .out12(x12w), .out13(x13w), .out14(x14w),
    .out15(x15w), .out16(x16w), .out17(x17w), .out18(x18w), .out19(x19w), .out20(x20w), .out21(x21w),
    .out22(x22w), .out23(x23w), .out24(x24w), .out25(x25w), .out26(x26w), .out27(x27w), .out28(x28w),
    .out29(x29w), .out30(x30w), .out31(x31w), .in(1'b1), .sel(WriteIndex));
  Multiplexer #(.width(32), .enable("false")) multiplexer_1 (
    .in0(x0q), .in1({32{1'b0}}), .out(multiplexer_1_out), .sel(x0w));
  Register #(.width(32)) x0 (.D(multiplexer_1_out), .en(RegWEn), .clk(clk), .Q(x0q));  // open: clr
  Multiplexer #(.width(32), .enable("false")) multiplexer_2 (
    .in0(sp), .in1(WriteData), .out(multiplexer_2_out), .sel(spw));
  Register #(.width(32)) x2 (.D(multiplexer_2_out), .en(RegWEn), .clk(clk), .Q(sp));  // open: clr
  Multiplexer #(.width(32), .enable("false")) multiplexer_3 (
    .in0(x4q), .in1(WriteData), .out(multiplexer_3_out), .sel(x4w));
  Register #(.width(32)) x4 (.D(multiplexer_3_out), .en(RegWEn), .clk(clk), .Q(x4q));  // open: clr
  Multiplexer #(.width(32), .enable("false")) multiplexer_4 (
    .in0(t1), .in1(WriteData), .out(multiplexer_4_out), .sel(t1w));
  Register #(.width(32)) x6 (.D(multiplexer_4_out), .en(RegWEn), .clk(clk), .Q(t1));  // open: clr
  Multiplexer #(.width(32), .enable("false")) multiplexer_5 (
    .in0(s0), .in1(WriteData), .out(multiplexer_5_out), .sel(s0w));
  Register #(.width(32)) x8 (.D(multiplexer_5_out), .en(RegWEn), .clk(clk), .Q(s0));  // open: clr
  Multiplexer #(.width(32), .enable("false")) multiplexer_6 (
    .in0(a0), .in1(WriteData), .out(multiplexer_6_out), .sel(a0w));
  Register #(.width(32)) x10 (.D(multiplexer_6_out), .en(RegWEn), .clk(clk), .Q(a0));  // open: clr
  Multiplexer #(.width(32), .enable("false")) multiplexer_7 (
    .in0(x12q), .in1(WriteData), .out(multiplexer_7_out), .sel(x12w));
  Register #(.width(32)) x12 (.D(multiplexer_7_out), .en(RegWEn), .clk(clk), .Q(x12q));  // open: clr
  Multiplexer #(.width(32), .enable("false")) multiplexer_8 (
    .in0(x11q), .in1(WriteData), .out(multiplexer_8_out), .sel(x11w));
  Register #(.width(32)) x11 (.D(multiplexer_8_out), .en(RegWEn), .clk(clk), .Q(x11q));  // open: clr
  Multiplexer #(.width(32), .enable("false")) multiplexer_9 (
    .in0(x13q), .in1(WriteData), .out(multiplexer_9_out), .sel(x13w));
  Register #(.width(32)) x13 (.D(multiplexer_9_out), .en(RegWEn), .clk(clk), .Q(x13q));  // open: clr
  Multiplexer #(.width(32), .enable("false")) multiplexer_10 (
    .in0(ra), .in1(WriteData), .out(multiplexer_10_out), .sel(raw));
  Register #(.width(32)) x1 (.D(multiplexer_10_out), .en(RegWEn), .clk(clk), .Q(ra));  // open: clr
  Multiplexer #(.width(32), .enable("false")) multiplexer_11 (
    .in0(x3q), .in1(WriteData), .out(multiplexer_11_out), .sel(x3w));
  Register #(.width(32)) x3 (.D(multiplexer_11_out), .en(RegWEn), .clk(clk), .Q(x3q));  // open: clr
  Multiplexer #(.width(32), .enable("false")) multiplexer_12 (
    .in0(t0), .in1(WriteData), .out(multiplexer_12_out), .sel(t0w));
  Register #(.width(32)) x5 (.D(multiplexer_12_out), .en(RegWEn), .clk(clk), .Q(t0));  // open: clr
  Multiplexer #(.width(32), .enable("false")) multiplexer_13 (
    .in0(t2), .in1(WriteData), .out(multiplexer_13_out), .sel(t2w));
  Register #(.width(32)) x7 (.D(multiplexer_13_out), .en(RegWEn), .clk(clk), .Q(t2));  // open: clr
  Multiplexer #(.width(32), .enable("false")) multiplexer_14 (
    .in0(s1), .in1(WriteData), .out(multiplexer_14_out), .sel(s1w));
  Register #(.width(32)) x9 (.D(multiplexer_14_out), .en(RegWEn), .clk(clk), .Q(s1));  // open: clr
  Multiplexer #(.width(32), .enable("false")) multiplexer_15 (
    .in0(x26q), .in1(WriteData), .out(multiplexer_15_out), .sel(x26w));
  Register #(.width(32)) x26 (.D(multiplexer_15_out), .en(RegWEn), .clk(clk), .Q(x26q));  // open: clr
  Multiplexer #(.width(32), .enable("false")) multiplexer_16 (
    .in0(x28q), .in1(WriteData), .out(multiplexer_16_out), .sel(x28w));
  Register #(.width(32)) x28 (.D(multiplexer_16_out), .en(RegWEn), .clk(clk), .Q(x28q));  // open: clr
  Multiplexer #(.width(32), .enable("false")) multiplexer_17 (
    .in0(x30q), .in1(WriteData), .out(multiplexer_17_out), .sel(x30w));
  Register #(.width(32)) x30 (.D(multiplexer_17_out), .en(RegWEn), .clk(clk), .Q(x30q));  // open: clr
  Multiplexer #(.width(32), .enable("false")) multiplexer_18 (
    .in0(x22q), .in1(WriteData), .out(multiplexer_18_out), .sel(x22w));
  Register #(.width(32)) x22 (.D(multiplexer_18_out), .en(RegWEn), .clk(clk), .Q(x22q));  // open: clr
  Multiplexer #(.width(32), .enable("false")) multiplexer_19 (
    .in0(x24q), .in1(WriteData), .out(multiplexer_19_out), .sel(x24w));
  Register #(.width(32)) x24 (.D(multiplexer_19_out), .en(RegWEn), .clk(clk), .Q(x24q));  // open: clr
  Multiplexer #(.width(32), .enable("false")) multiplexer_20 (
    .in0(x23q), .in1(WriteData), .out(multiplexer_20_out), .sel(x23w));
  Register #(.width(32)) x23 (.D(multiplexer_20_out), .en(RegWEn), .clk(clk), .Q(x23q));  // open: clr
  Multiplexer #(.width(32), .enable("false")) multiplexer_21 (
    .in0(x25q), .in1(WriteData), .out(multiplexer_21_out), .sel(x25w));
  Register #(.width(32)) x25 (.D(multiplexer_21_out), .en(RegWEn), .clk(clk), .Q(x25q));  // open: clr
  Multiplexer #(.width(32), .enable("false")) multiplexer_22 (
    .in0(x27q), .in1(WriteData), .out(multiplexer_22_out), .sel(x27w));
  Register #(.width(32)) x27 (.D(multiplexer_22_out), .en(RegWEn), .clk(clk), .Q(x27q));  // open: clr
  Multiplexer #(.width(32), .enable("false")) multiplexer_23 (
    .in0(x29q), .in1(WriteData), .out(multiplexer_23_out), .sel(x29w));
  Register #(.width(32)) x29 (.D(multiplexer_23_out), .en(RegWEn), .clk(clk), .Q(x29q));  // open: clr
  Multiplexer #(.width(32), .enable("false")) multiplexer_24 (
    .in0(x31q), .in1(WriteData), .out(multiplexer_24_out), .sel(x31w));
  Register #(.width(32)) x31 (.D(multiplexer_24_out), .en(RegWEn), .clk(clk), .Q(x31q));  // open: clr
  Multiplexer #(.width(32), .enable("false")) multiplexer_25 (
    .in0(x20q), .in1(WriteData), .out(multiplexer_25_out), .sel(x20w));
  Register #(.width(32)) x20 (.D(multiplexer_25_out), .en(RegWEn), .clk(clk), .Q(x20q));  // open: clr
  Multiplexer #(.width(32), .enable("false")) multiplexer_26 (
    .in0(x18q), .in1(WriteData), .out(multiplexer_26_out), .sel(x18w));
  Multiplexer #(.select(5), .width(32), .enable("false")) multiplexer_27 (
    .in0(x0q), .in1(ra), .in2(sp), .in3(x3q), .in4(x4q), .in5(t0), .in6(t1), .in7(t2), .in8(s0), .in9(s1),
    .in10(a0), .in11(x11q), .in12(x12q), .in13(x13q), .in14(x14q), .in15(x15q), .in16(x16q), .in17(x17q),
    .in18(x18q), .in19(x19q), .in20(x20q), .in21(x21q), .in22(x22q), .in23(x23q), .in24(x24q), .in25(x25q),
    .in26(x26q), .in27(x27q), .in28(x28q), .in29(x29q), .in30(x30q), .in31(x31q), .out(ReadData1),
    .sel(ReadIndex1));
  Register #(.width(32)) x18 (.D(multiplexer_26_out), .en(RegWEn), .clk(clk), .Q(x18q));  // open: clr
  Multiplexer #(.width(32), .enable("false")) multiplexer_28 (
    .in0(x21q), .in1(undriven), .out(multiplexer_28_out), .sel(x21w));
  Register #(.width(32)) x21 (.D(multiplexer_28_out), .en(RegWEn), .clk(clk), .Q(x21q));  // open: clr
  Multiplexer #(.width(32), .enable("false")) multiplexer_29 (
    .in0(x19q), .in1(WriteData), .out(multiplexer_29_out), .sel(x19w));
  Register #(.width(32)) x19 (.D(multiplexer_29_out), .en(RegWEn), .clk(clk), .Q(x19q));  // open: clr
  // Multiplexer #(.width(32), .enable("false")) multiplexer_30: pin names not known; wires that end beside it: x14w, x14q, multiplexer_30_p3, WriteData
  Register #(.width(32)) x14 (.D(multiplexer_30_p3), .en(RegWEn), .clk(clk), .Q(x14q));  // open: clr
  Multiplexer #(.width(32), .enable("false")) multiplexer_31 (
    .in0(x16q), .in1(WriteData), .out(multiplexer_31_out), .sel(x16w));
  Register #(.width(32)) x16 (.D(multiplexer_31_out), .en(RegWEn), .clk(clk), .Q(x16q));  // open: clr
  Multiplexer #(.select(5), .width(32), .enable("false")) multiplexer_32 (
    .in0(x0q), .in1(ra), .in2(sp), .in3(x3q), .in4(x4q), .in5(t0), .in6(t1), .in7(t2), .in8(s0), .in9(s1),
    .in10(a0), .in11(x11q), .in12(x12q), .in13(x13q), .in14(x14q), .in15(x15q), .in16(x16q), .in17(x17q),
    .in18(x18q), .in19(x19q), .in20(x20q), .in21(x21q), .in22(x22q), .in23(x23q), .in24(x24q), .in25(x25q),
    .in26(x26q), .in27(x27q), .in28(x28q), .in29(x29q), .in30(x30q), .in31(x31q), .out(ReadData2),
    .sel(ReadIndex2));
  // Multiplexer #(.width(32), .enable("false")) multiplexer_33: pin names not known; wires that end beside it: x15w, x15q, multiplexer_33_p3, WriteData
  Register #(.width(32)) x15 (.D(multiplexer_33_p3), .en(RegWEn), .clk(clk), .Q(x15q));  // open: clr
  Multiplexer #(.width(32), .enable("false")) multiplexer_34 (
    .in0(x17q), .in1(WriteData), .out(multiplexer_34_out), .sel(x17w));
  Register #(.width(32)) x17 (.D(multiplexer_34_out), .en(RegWEn), .clk(clk), .Q(x17q));  // open: clr

  // Notes on the sheet:
  //   INPUTS to your circuit
  //   DON'T CHANGE THE LOCATIONS OF THE INPUTS AND OUTPUTS!
  //   These are DEBUG/TEST outputs from your circuit.
  //   OUTPUTS from your circuit
endmodule
